# Fritzing sketch 1-blinky (saved by Fritzing 1.0.5)
breadboards: 1

parts:
  MCU1 = Raspberry Pi Zero
  R4 = Resistor [tolerance=±5% power=0.25W resistance=100 package=THT]
  LED1 = smd LED [color="Red (633nm)" package="1206 [SMD]"]

nets:
  N1: MCU1.pin_6, LED1.cathode
  N2: MCU1.pin_13, R4.Pin_0
  N3: R4.Pin_1, LED1.anode
