# Fritzing sketch 2-motor-bm (saved by Fritzing 1.0.5)
breadboards: 1

parts:
  Q1 = NPN-Transistor [package="TO92 [THT]"]
  R1 = Resistor [tolerance=±5% power=0.25W resistance=2.2k package=THT]
  R2 = Resistor [tolerance=±5% power=0.25W resistance=1000 package=THT]
  M1 = DC Motor [voltage_(max)=6V voltage_(min)=3V]
  R3 = Resistor [tolerance=±5% power=0.25W resistance=1000 package=THT]
  D1 = Diode [package=diode-1n4148]
  U1 = ESP32S-HiLetgo [part_number=ESP32S-HiLetgo]
  R4 = Rotary Potentiometer (Small) [maximum_resistance=10kΩ knob_status=50% power=0.5W package=THT]

nets:
  N1: Q1.E, R1.Pin_0, U1.GND, R4.leg1
  N2: Q1.B, M1.pin_1, D1.A
  N3: Q1.C, R3.Pin_1
  N4: R1.Pin_1, R2.Pin_0, U1.GPIO32
  N5: R2.Pin_1, R4.wiper
  N6: M1.pin_2, D1.C, U1.VIN, R4.leg2
  N7: R3.Pin_0, U1.GPIO18

custom parts:
  ESP32S-HiLetgo: HiLetgo ESP-WROOM-32 ESP32 ESP-32S Development Board 2.4GHz Dual-Mode WiFi + Bluetooth Dual Cores Microcontroller The ESP32 integrated with Antenna switches, RF Balun, power amplifiers, low-noise amplifiers, filters, and management modules, and the entire solution occupies the least area of PCB. 2.4 GHz Wi-Fi plus Bluetooth dual-mode chip, with TSMC Ultra-low power consumption 40nm technology,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
