# Fritzing sketch 3-pid-bm (saved by Fritzing 1.0.5)
breadboards: 1

parts:
  Q1 = NPN-Transistor [package="TO92 [THT]"]
  R1 = Resistor [tolerance=±5% power=0.25W resistance=2.2k package=THT]
  R2 = Resistor [tolerance=±5% power=0.25W resistance=1000 package=THT]
  DS1 = DS18B20 1-Wire Temperature Sensor [part_number=DS18B20]
  M1 = DC Motor [voltage_(max)=6V voltage_(min)=3V]
  R3 = Resistor [tolerance=±5% power=0.25W resistance=1000 package=THT]
  D1 = Diode [package=diode-1n4148]
  U1 = ESP32S-HiLetgo [part_number=ESP32S-HiLetgo]

nets:
  GND: Q1.E, R1.Pin_0, DS1.GND, U1.GND
  N1: Q1.B, M1.pin_1, D1.A
  N2: Q1.C, R3.Pin_1
  N3: R1.Pin_1, R2.Pin_0, U1.GPIO25
  N4: R2.Pin_1, DS1.DQ
  VDD: DS1.VDD, M1.pin_2, D1.C, U1.VIN
  N5: R3.Pin_0, U1.GPIO17

custom parts:
  ESP32S-HiLetgo: HiLetgo ESP-WROOM-32 ESP32 ESP-32S Development Board 2.4GHz Dual-Mode WiFi + Bluetooth Dual Cores Microcontroller The ESP32 integrated with Antenna switches, RF Balun, power amplifiers, low-noise amplifiers, filters, and management modules, and the entire solution occupies the least area of PCB. 2.4 GHz Wi-Fi plus Bluetooth dual-mode chip, with TSMC Ultra-low power consumption 40nm technology,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
