# Fritzing sketch 3-pid (saved by Fritzing 1.0.5)
breadboards: 1

parts:
  Q1 = NPN-Transistor [package="TO92 [THT]"]
  M1 = DC Motor [voltage_(max)=6V voltage_(min)=3V]
  R3 = Resistor [tolerance=±5% power=0.25W resistance=1000 package=THT]
  D1 = Diode [package=diode-1n4148]
  MCU1 = Raspberry Pi Zero
  Adafruit_ADS7830_8-Channel_8-Bit_ADC1 = Adafruit ADS7830 8-Channel 8-Bit ADC [part_number=#5836]
  DS2 = DS18B20 1-Wire Temperature Sensor [part_number=DS18B20]

nets:
  GND: Q1.E, MCU1.pin_6, MCU1.pin_20, Adafruit_ADS7830_8-Channel_8-Bit_ADC1.GND, DS2.GND
  N1: Q1.B, M1.pin_1, D1.A
  N2: Q1.C, R3.Pin_1
  VCC: M1.pin_2, D1.C, MCU1.pin_2, MCU1.pin_4, Adafruit_ADS7830_8-Channel_8-Bit_ADC1.VCC, Adafruit_ADS7830_8-Channel_8-Bit_ADC1.REF, DS2.VDD
  N3: R3.Pin_0, MCU1.pin_33
  N4: MCU1.pin_3, Adafruit_ADS7830_8-Channel_8-Bit_ADC1.SDA
  N5: MCU1.pin_5, Adafruit_ADS7830_8-Channel_8-Bit_ADC1.SCL
  N6: Adafruit_ADS7830_8-Channel_8-Bit_ADC1.A0, DS2.DQ

custom parts:
  Adafruit ADS7830 8-Channel 8-Bit ADC: Many microcontrollers have ADCs these days, for reading analog/resistive sensors like potentiometers, thermistors, LDR light sensors, etc. but sometimes you need MOAR! Or maybe you're using a single board computer like a Raspberry Pi that has no ADCs at all! The Adafruit ADS7830 8-Channel 8-Bit ADC with I2C is an affordable 8-channel ADC with I2C interface, so it's easy to include with any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
